# Fritzing sketch beer_fermentation_monitoring (saved by Fritzing 0.9.3b)
circuit board: 8.46667cm x 5.64444cm

parts:
  ESP12E1 = ESP 12E
  R2 = Resistor [tolerance=±5% resistance=10k package=THT]
  T2 = LM35 Temperature Sensor [package="TO92 [THT]"]
  J1 = female pin header, 2 pins [form="♀ (female)"]
  J2 = female pin header, 2 pins [form="♀ (female)"]
  J3 = female pin header, 2 pins [form="♀ (female)"]
  J5- = female pin header, 6 pins [form="♀ (female)"]
  S1_firmware = Toggle Switch [package=THT]
  Power_3_3v = Power plug
  R4 = Resistor [tolerance=±5% resistance=470 package=THT]
  R5 = Resistor [tolerance=±5% resistance=10k package=THT]
  R6 = Resistor [tolerance=±5% resistance=10k package=THT]
  S2_power = Toggle Switch [package=THT]
  R7 = Resistor [tolerance=±5% resistance=10k package=THT]
  R8 = Resistor [tolerance=±5% resistance=10k package=THT]
  J4+ = female pin header, 6 pins [form="♀ (female)"]
  R9 = Resistor [tolerance=±5% resistance=4.7k package=THT]

nets:
  N1: ESP12E1.GPIO5, J1.pin2, R9.Pin_1
  N2: ESP12E1.GPIO0, S1_firmware.COM, R8.Pin_1
  N3: ESP12E1.GPIO2, R7.Pin_0
  N4: ESP12E1.GPIO15, R5.Pin_0
  N5: ESP12E1.GND, J5-.pin3
  N6: ESP12E1.VCC, J4+.pin2
  N7: ESP12E1.GPIO16, R4.Pin_1
  N8: ESP12E1.EN, R2.Pin_1
  N9: ESP12E1.RST, R4.Pin_0, R6.Pin_0
  N10: R2.Pin_0, J4+.pin3
  N11: T2.+Vs, J3.pin1
  N12: T2.Vout, J1.pin1
  N13: T2.GND, J2.pin1
  N14: J2.pin2, J4+.pin1, R9.Pin_0
  N15: J3.pin2, J5-.pin1
  N16: J5-.pin2, R5.Pin_1
  N17: J5-.pin5, S1_firmware.L1
  N18: J5-.pin6, Power_3_3v.GND
  N19: Power_3_3v.VCC, S2_power.COM
  N20: R6.Pin_1, J4+.pin4
  N21: S2_power.L1, J4+.pin6
  N22: R7.Pin_1, R8.Pin_0, J4+.pin5

notes:
  usb-ttl
  rx
  tx
  d5
  deep sleep

custom parts:
  ESP 12E: ESP 12e module with spi interface and wifi connection
